# Fritzing sketch LoRaNODE (saved by Fritzing 0.9.3b)
circuit board: 8.46667cm x 5.64444cm
breadboards: 1

parts:
  V_Raw = Battery
  Arduino = Arduino Pro Mini v13 [part_number=Arduino]
  Temperature_Sensor = SHT1x-Breakout [part_number="Temperature Sensor"]
  R1 = Resistor [tolerance=±5% resistance=100k package=THT]
  R2 = Resistor [tolerance=±5% resistance=100k package=THT]
  R3 = Resistor [tolerance=±5% resistance=47k package=THT]
  R4 = Resistor [tolerance=±5% resistance=47k package=THT]
  D1 = Rectifier Diode [part_number=1N4001 package="300 mil [THT]"]
  C2 = Electrolytic Capacitor [capacitance=1µF package="100 mil [THT, electrolytic]"]
  U1 = COPERNICUS-DIP [package=copernicus-dip]
  S1 = Toggle Switch [package=THT]

nets (from the breadboard view):
  GND: V_Raw.-, Arduino.GND, Temperature_Sensor.GND, R4.Pin_1, D1.anode, C2.+, U1.TXD-B, S1.COM
  N1: Arduino.A4, Temperature_Sensor.DATA, R1.Pin_1
  N2: Arduino.A5, Temperature_Sensor.SCK, R2.Pin_1
  N3: Arduino.RAW, R3.Pin_0, C2.-, S1.L1
  VCC: Arduino.VCC, Temperature_Sensor.VCC, R1.Pin_0, R2.Pin_0, U1.RESERVED5
  N4: Arduino.A0, R3.Pin_1, R4.Pin_0, D1.cathode
  N5: Arduino.D8, U1.PPS
  N6: Arduino.D7, U1.RESERVED4
  N7: Arduino.D2, U1.RXD-B
